# Fritzing sketch DC-Scheme (saved by Fritzing 0.9.4)
breadboards: 1

parts:
  BT1 = Bluetooth HC-06u [package=THT]
  Part1 = Arduino Uno (Rev3) - ICSP
  J1 = Basic Servo
  LED1 = smd LED [color="Green (565nm)" package="0603 [SMD]"]
  R1 = Resistor [tolerance=±5% resistance=220 package="0402 [SMD]"]

nets:
  VCC: BT1.VCC, Part1.5V, J1.vcc
  GND: BT1.GND, Part1.GND, J1.gnd, R1.Pin_0
  N1: BT1.TXD, Part1.D2
  N2: BT1.RXD, Part1.D3_PWM
  N3: Part1.D4, LED1.anode
  N4: Part1.D5_PWM, J1.pulse
  N5: LED1.cathode, R1.Pin_1

custom parts:
  Bluetooth HC-06u: Bluetooth HC-06 - face up, pins down 16.5mm x 37.5mm PCB
