# Fritzing sketch RH - Schema (saved by Fritzing 0.9.3b)
breadboards: 1

parts:
  hc-sr2 = hc-sr04
  LED2 = LED - 5mm [color="Green (570nm)" package="5 mm [THT]"]
  U2 = NodeMCU V1.0
  R2 = Resistor [tolerance=±5% resistance=220 package=THT]

nets:
  VCC: hc-sr2.VCC, U2.Vin
  N1: hc-sr2.Trig, U2.D6
  N2: hc-sr2.Echo, U2.D7
  GND: hc-sr2.GND, U2.GND, R2.Pin_0
  N3: LED2.cathode, R2.Pin_1
  N4: LED2.anode, U2.D1

custom parts:
  NodeMCU V1.0: ESP8266 based NodeMCU
